# Fritzing sketch Sketch (saved by Fritzing 0.9.2b)
breadboards: 1

parts:
  RHT1 = Humidity and Temperature Sensor RHT03
  LED1 = smd LED [color="Green (555nm)" package="0805 [SMD]"]
  Componente1 = Arduino Uno (Rev3) - ICSP
  U1 = SHT1x Humdity Sensor [package=sht1x]
  T2 = TMP36 Temperature Sensor [package="TO92 [THT]"]
  Lhi3 = LHi958 [package=to-39]
  R1 = Resistor [tolerance=±5% resistance=10k package="0603 [SMD]"]
  R2 = Resistor [tolerance=±5% resistance=4.7k package="0603 [SMD]"]
  R5 = Resistor [tolerance=±5% resistance=1k package="0603 [SMD]"]

nets:
  VCC: RHT1.Vcc, Componente1.5V, U1.VDD, T2.+Vs, Lhi3.D
  N1: RHT1.Data-signal, Componente1.D4, R1.Pin_0
  GND: RHT1.GND_2, LED1.cathode, Componente1.GND, U1.GND, Lhi3.GND
  N2: LED1.anode, R5.Pin_1
  N3: Componente1.A0, U1.DATA
  N4: Componente1.D3_PWM, R5.Pin_0
  N5: Componente1.D5_PWM, T2.Vout, R2.Pin_0
  N6: Componente1.D6_PWM, Lhi3.n.a.

notes:
  led
  DHT11
  DS18b20
  PIR
  Soil
  Humidity
